# Fritzing sketch Diagrama SensorIR-ServoMotor (saved by Fritzing 0.9.10b)
breadboards: 1

parts:
  Mod1 = KY-022 Infrared Receiver Module [package="Breakout board"]
  J1 = Basic Servo
  ESP32_-_Back1 = ESP32 - CAM

nets:
  N1: Mod1.-, J1.gnd, ESP32_-_Back1.GND#7
  VIN: Mod1.Vin, J1.vcc, ESP32_-_Back1.5V
  N2: Mod1.S, ESP32_-_Back1.GPIO15
  N3: ESP32_-_Back1.GPIO0, ESP32_-_Back1.GND#12

custom parts:
  KY-022 Infrared Receiver Module: KY-022 IR receiver module, reacts to 38kHz infrared light.
  ESP32 - CAM: The ESP32-CAM has a very competitive small-size camera module that can operate independently as a minimum system with a footprint of only 27*40.5*4.5mm and a deep sleep current of up to 6mA.
