# Fritzing sketch Diagrama SensorIR-ServoMotor-ArduinoUno-Esp32Cam (saved by Fritzing 0.9.10b)
breadboards: 1

parts:
  Mod1 = ESP32 - CAM
  Componente2 = Arduino Uno (Rev3) - ICSP
  J3 = Basic Servo
  J4 = Basic Servo
  Mod2 = KY-022 Infrared Receiver Module [package="Breakout board"]
  LED1 = LED - 5mm [color="White (4500K)" current=0.030 package="5 mm [THT]"]
  LED2 = LED - 5mm [color="Green (555nm)" current=30mA package="5 mm [THT]"]
  LED3 = LED - 5mm [color="Blue (430nm)" current=0.030 package="5 mm [THT]"]
  LED4 = LED - 5mm [color="Red (633nm)" current=0.030 package="5 mm [THT]"]
  R1 = Resistor [tolerance=±5% power=0.25 resistance=220 package=THT]
  R2 = Resistor [tolerance=±5% power=0.25 resistance=220 package=THT]
  R3 = Resistor [tolerance=±5% power=0.25 resistance=220 package=THT]
  R4 = Resistor [tolerance=±5% power=0.25 resistance=220 package=THT]
  Tiny_RTC1 = Tiny RTC

nets:
  5V: Mod1.5V, Componente2.5V, J4.vcc, Mod2.Vin, Tiny_RTC1.VCC
  GND: Mod1.GND, Componente2.GND, J4.gnd, Mod2.-, R1.Pin_1, R2.Pin_1, R3.Pin_1, R4.Pin_1, Tiny_RTC1.GND
  N1: Mod1.VOT, Componente2.D0/RX
  N2: Mod1.VOR, Componente2.D1/TX
  N3: Componente2.A4/SDA, Tiny_RTC1.SDA
  N4: Componente2.A5/SCL, Tiny_RTC1.SCL
  N5: Componente2.D8, LED1.anode
  N6: Componente2.D2, J3.pulse
  N7: Componente2.D3_PWM, Mod2.S
  N8: Componente2.D4, J4.pulse
  N9: Componente2.D5_PWM, LED2.anode
  N10: Componente2.D6_PWM, LED4.anode
  N11: Componente2.D7, LED3.anode
  N12: LED1.cathode, R1.Pin_0
  N13: LED2.cathode, R2.Pin_0
  N14: LED3.cathode, R4.Pin_0
  N15: LED4.cathode, R3.Pin_0

custom parts:
  ESP32 - CAM: The ESP32-CAM has a very competitive small-size camera module that can operate independently as a minimum system with a footprint of only 27*40.5*4.5mm and a deep sleep current of up to 6mA.
  KY-022 Infrared Receiver Module: KY-022 IR receiver module, reacts to 38kHz infrared light.
  Tiny RTC: Tiny RTC I2C module DS1370Z RTC and AT24C32 EEPROM
